# Fritzing sketch Schematic (saved by Fritzing 0.9.6b)
breadboards: 1

parts:
  Part1 = Arduino Uno (Rev3)
  LCD1 = LCD screen
  RHT1 = Humidity and Temperature Sensor RHT03
  LED1 = RGB LED (com. cathode, rgb) [package="5 mm [THT]"]
  U1 = PCF8574 [package="DIP16 [THT]"]
  S1 = Momentary Switch [package=ksa_sealed_tac_switch]

nets (from the schematic view):
  N1: Part1.A4/SDA, U1.SDA
  N2: Part1.A5/SCL, U1.SCL
  GND: Part1.GND, RHT1.GND_2, LED1.common_cathode, U1.GND, S1.4
  N3: Part1.D2, LED1.blue_anode
  N4: Part1.D3_PWM, LED1.green_anode
  N5: Part1.D4, LED1.red_anode
  N6: Part1.D5_PWM, RHT1.Data-signal
  5V: Part1.5V, U1.VCC, S1.2
  N7: LCD1.RS, U1.P0
  N8: LCD1.R/W, U1.P1
  N9: LCD1.E, U1.P2
  N10: LCD1.DB4, U1.P4
  N11: LCD1.DB5, U1.P5
  N12: LCD1.DB6, U1.P6
  N13: LCD1.DB7, U1.P7
  N14: RHT1.Vcc, S1.1
